# Fritzing sketch JarvisDesk_WeMosD1Mini_v2 (saved by Fritzing 0.9.5d)
circuit board: 8.22632cm x 3.38789cm
breadboards: 1

parts:
  U1 = RJ45 Jack [package=rj45-8]
  U2 = RJ45 Jack [package=rj45-8]
  WeMos_D1_Mini1 = WeMos D1 Mini

nets:
  N1: U1.1, U2.1, WeMos_D1_Mini1.D5
  N2: U1.2, U2.2, WeMos_D1_Mini1.D2
  N3: U1.3, U2.3, WeMos_D1_Mini1.G
  N4: U1.4, U2.4, WeMos_D1_Mini1.D1
  N5: U1.5, U2.5, WeMos_D1_Mini1.5V
  N6: U1.6, U2.6, WeMos_D1_Mini1.D0
  N7: U1.7, U2.7, WeMos_D1_Mini1.D6
  N8: U1.8, U2.8, WeMos_D1_Mini1.D7

notes:
  Robodesk
  phord/Jarvis
  Jarvis v2.1
  Jan 2022
  github.com/
